# Fritzing sketch Centrale-Commande (saved by Fritzing 0.9.2b)
breadboards: 1

parts:
  Nano1 = Arduino Nano v2.3
  U1 = ENCODER-QUADRATURE [package=encoder-16mm-quad]  # not connected
  Composant1 = E-Paper Eval Board  # not connected
  J1 = Generic female header - 3 pins [form="♀ (female)" package=THT]  # not connected
  SFH620A = TLP621 [package=THT]
  R1 = Resistor [tolerance=±5% resistance=1k package=THT]
  R2 = Resistor [tolerance=±5% resistance=4.7k package=THT]
  V2 = DC Power [voltage=5]
  TELEINFO = Screw terminal - 2 pins [package=THT]
  J3 = screw terminal, 4 pins
  D1 = Rectifier Diode [part_number=1N4007 package="300 mil [THT]"]
  U2 = Optocoupler [part_number=MOC3041M package=THT]
  U3 = Optocoupler [part_number=MOC3041M package=THT]
  U4 = Optocoupler [part_number=MOC3041M package=THT]
  U5 = Optocoupler [part_number=MOC3041M package=THT]
  R3 = Resistor [tolerance=±5% resistance=220 package=THT]
  R4 = Resistor [tolerance=±5% resistance=220 package=THT]
  R5 = Resistor [tolerance=±5% resistance=220 package=THT]
  R6 = Resistor [tolerance=±5% resistance=220 package=THT]
  LED2 = LED - 5mm [color="Red (633nm)" package="5 mm [THT]"]
  LED3 = LED - 5mm [color="Red (633nm)" package="5 mm [THT]"]
  LED4 = LED - 5mm [color="Red (633nm)" package="5 mm [THT]"]
  LED5 = LED - 5mm [color="Red (633nm)" package="5 mm [THT]"]
  LED6 = LED - 5mm [color="Red (633nm)" package="5 mm [THT]"]
  U6 = RJ45 Jack [package=rj45-8]  # not connected

nets:
  N1: Nano1.GND, SFH620A.Pin_3, V2.V-, R3.Pin_0, R4.Pin_0, R5.Pin_0, R6.Pin_0
  N2: Nano1.D5, SFH620A.Pin_4, LED6.cathode
  N3: Nano1.A7, LED4.anode
  N4: Nano1.A6, LED2.anode
  N5: Nano1.A5, LED5.anode
  N6: Nano1.A4, LED3.anode
  N7: Nano1.VIN, R2.Pin_1, V2.V+
  N8: SFH620A.Pin_1, TELEINFO.pin2
  N9: SFH620A.Pin_2, R1.Pin_1
  N10: R1.Pin_0, TELEINFO.pin1
  N11: R2.Pin_0, LED6.anode
  N12: J3.pin1, U4.Pin_5
  N13: J3.pin2, U2.Pin_5
  N14: J3.pin3, U5.Pin_5
  N15: J3.pin4, U3.Pin_5
  N16: D1.cathode, U2.Pin_6, U3.Pin_6, U4.Pin_6, U5.Pin_6
  N17: U2.Pin_1, LED2.cathode
  N18: U2.Pin_2, R3.Pin_1
  N19: U3.Pin_1, LED5.cathode
  N20: U3.Pin_2, R4.Pin_1
  N21: U4.Pin_1, LED3.cathode
  N22: U4.Pin_2, R6.Pin_1
  N23: U5.Pin_1, LED4.cathode
  N24: U5.Pin_2, R5.Pin_1

custom parts:
  Generic female header - 3 pins: Generic female header
