# Fritzing sketch Centrale-DIN (saved by Fritzing 0.9.2b)
breadboards: 1

parts:
  SFH620A = TLP621 [package=THT]
  R1 = Resistor [tolerance=±5% resistance=1k package=THT]
  R2 = Resistor [tolerance=±5% resistance=4.7k package=THT]
  V2 = DC Power [voltage=5]
  TELEINFO = Screw terminal - 2 pins [package=THT]
  J3 = screw terminal, 4 pins
  D1 = Rectifier Diode [part_number=1N4007 package="300 mil [THT]"]
  U2 = Optocoupler [part_number=MOC3041M package=THT]
  U3 = Optocoupler [part_number=MOC3041M package=THT]
  U4 = Optocoupler [part_number=MOC3041M package=THT]
  U5 = Optocoupler [part_number=MOC3041M package=THT]
  R3 = Resistor [tolerance=±5% resistance=220 package=THT]
  R4 = Resistor [tolerance=±5% resistance=220 package=THT]
  R5 = Resistor [tolerance=±5% resistance=220 package=THT]
  R6 = Resistor [tolerance=±5% resistance=220 package=THT]
  LED2 = LED - 5mm [color="Red (633nm)" package="5 mm [THT]"]
  LED3 = LED - 5mm [color="Red (633nm)" package="5 mm [THT]"]
  LED4 = LED - 5mm [color="Red (633nm)" package="5 mm [THT]"]
  LED5 = LED - 5mm [color="Red (633nm)" package="5 mm [THT]"]
  LED6 = LED - 5mm [color="Red (633nm)" package="5 mm [THT]"]
  U6 = RJ45 Jack [package=rj45-8]

nets:
  N1: SFH620A.Pin_1, TELEINFO.pin2
  N2: SFH620A.Pin_2, R1.Pin_1
  N3: SFH620A.Pin_4, LED6.cathode, U6.6
  N4: SFH620A.Pin_3, V2.V-, U6.7
  N5: R1.Pin_0, TELEINFO.pin1
  N6: R2.Pin_0, LED6.anode
  N7: R2.Pin_1, V2.V+, U6.8
  N8: J3.pin1, U4.Pin_5
  N9: J3.pin2, U2.Pin_5
  N10: J3.pin3, U5.Pin_5
  N11: J3.pin4, U3.Pin_5
  N12: D1.cathode, U2.Pin_6, U3.Pin_6, U4.Pin_6, U5.Pin_6
  N13: U2.Pin_1, LED2.cathode
  N14: U2.Pin_2, R3.Pin_1
  N15: U3.Pin_1, LED5.cathode
  N16: U3.Pin_2, R4.Pin_1
  N17: U4.Pin_1, LED3.cathode
  N18: U4.Pin_2, R6.Pin_1
  N19: U5.Pin_1, LED4.cathode
  N20: U5.Pin_2, R5.Pin_1
  N21: R3.Pin_0, R4.Pin_0, R5.Pin_0, R6.Pin_0
  N22: LED2.anode, U6.2
  N23: LED3.anode, U6.4
  N24: LED4.anode, U6.1
  N25: LED5.anode, U6.3
