# Fritzing sketch Projet Fritzing (saved by Fritzing 0.9.2b)
circuit board: 3.87101cm x 3.49204cm
breadboards: 1

parts:
  RHT03 = Humidity and Temperature Sensor RHT03
  ATTINY85 = attiny85 [package=dip]
  +9V = BC9VPC [package=bc9vpc]
  RF433 = Generic female header - 3 pins [form="♀ (female)" package=THT]
  R2 = Resistor [tolerance=±5% resistance=10k package=THT]
  R1 = Resistor [tolerance=±5% resistance=220 package=THT]
  LED1 = LEDs [package=led10mm]

nets (from the schematic view):
  VCC: RHT03.Vcc, ATTINY85.Pin_8, +9V.V+, RF433.+5v, R2.Pin_1
  N1: RHT03.Data-signal, ATTINY85.Pin_5, R2.Pin_0
  N2: RHT03.GND_2, RF433.GND
  N3: ATTINY85.Pin_4, +9V.V-, R1.Pin_0
  N4: ATTINY85.Pin_6, RF433.DATA
  N5: ATTINY85.Pin_7, LED1.A
  N6: R1.Pin_1, LED1.C

custom parts:
  Generic female header - 3 pins: Generic female header
